// Logisim project DinoGame_cactus_and_bird.circ as structural Verilog: 1 circuit, main circuit bird
module bird (
  output [31:0] out_1,
  output [31:0] out_2,
  output [31:0] out_3,
  output [31:0] out_4,
  output [31:0] out_5,
  output [31:0] out_6,
  output [31:0] out_7,
  output [31:0] out_8,
  output [31:0] out_9,
  output [31:0] out_10,
  output [31:0] out_11,
  output [31:0] out_12,
  output [31:0] out_13,
  output [31:0] out_14,
  output [31:0] out_15,
  output [31:0] out_16,
  output [31:0] out_17,
  output [31:0] out_18
);

  DotMatrix #(.matrixcols(9), .matrixrows(32)) dotmatrix_1 (
    .col0(32'h8), .col1(32'h18), .col2(32'h8), .col3(32'h3c), .col4(32'h7c), .col5(32'h7c), .col6(32'h38),
    .col7(32'h8), .col8(32'h14));
  DotMatrix #(.matrixcols(9), .matrixrows(32)) dotmatrix_2 (
    .col0(32'h8), .col1(32'h18), .col2(32'h8), .col3(32'he), .col4(32'hf), .col5(32'hf), .col6(32'he),
    .col7(32'h8), .col8(32'h14));

  assign out_1 = 32'h8;
  assign out_2 = 32'h18;
  assign out_3 = 32'h8;
  assign out_4 = 32'h3c;
  assign out_5 = 32'h7c;
  assign out_6 = 32'h7c;
  assign out_7 = 32'h38;
  assign out_8 = 32'h8;
  assign out_9 = 32'h14;
  assign out_10 = 32'h8;
  assign out_11 = 32'h18;
  assign out_12 = 32'h8;
  assign out_13 = 32'he;
  assign out_14 = 32'hf;
  assign out_15 = 32'hf;
  assign out_16 = 32'he;
  assign out_17 = 32'h8;
  assign out_18 = 32'h14;
endmodule
