// Logisim project GoogleDino_bird.circ as structural Verilog: 2 circuits, main circuit bird
module bird (
  output [31:0] out_1,
  output [31:0] out_2,
  output [31:0] out_3,
  output [31:0] out_4,
  output [31:0] out_5,
  output [31:0] out_6,
  output [31:0] out_7,
  output [31:0] out_8,
  output [31:0] out_9,
  output [31:0] out_10,
  output [31:0] out_11,
  output [31:0] out_12,
  output [31:0] out_13,
  output [31:0] out_14,
  output [31:0] out_15,
  output [31:0] out_16,
  output [31:0] out_17,
  output [31:0] out_18
);

  DotMatrix #(.matrixcols(9), .matrixrows(32)) dotmatrix_1 (
    .col0(32'h8), .col1(32'h18), .col2(32'h8), .col3(32'h3c), .col4(32'h7c), .col5(32'h7c), .col6(32'h38),
    .col7(32'h8), .col8(32'h14));
  DotMatrix #(.matrixcols(9), .matrixrows(32)) dotmatrix_2 (
    .col0(32'h8), .col1(32'h18), .col2(32'h8), .col3(32'he), .col4(32'hf), .col5(32'hf), .col6(32'he),
    .col7(32'h8), .col8(32'h14));

  assign out_1 = 32'h8;
  assign out_2 = 32'h18;
  assign out_3 = 32'h8;
  assign out_4 = 32'h3c;
  assign out_5 = 32'h7c;
  assign out_6 = 32'h7c;
  assign out_7 = 32'h38;
  assign out_8 = 32'h8;
  assign out_9 = 32'h14;
  assign out_10 = 32'h8;
  assign out_11 = 32'h18;
  assign out_12 = 32'h8;
  assign out_13 = 32'he;
  assign out_14 = 32'hf;
  assign out_15 = 32'hf;
  assign out_16 = 32'he;
  assign out_17 = 32'h8;
  assign out_18 = 32'h14;
endmodule

module birds_control (
  input  gen_obst,
  input  [3:0] speed,
  input  pause,
  output [31:0] up,
  output [31:0] down,
  output birds_clk
);

  wire common_speed_1_clk, controlled_buffer_1_out, counter_1_carry, multiplexer_1_out, not_1_out, not_2_out,
       not_3_out, t_ff_1_q;
  wire [1:0] random_2_out;
  wire [3:0] counter_1_q, divider_1_rem, random_1_out;
  wire [31:0] bird_1_out_1, bird_1_out_2, bird_1_out_3, bird_1_out_4, bird_1_out_5, bird_1_out_6,
       bird_1_out_7, bird_1_out_8, bird_1_out_9, bird_1_out_10, bird_1_out_11, bird_1_out_12, bird_1_out_13,
       bird_1_out_14, bird_1_out_15, bird_1_out_16, bird_1_out_17, bird_1_out_18, pull_resistor_3_node,
       pull_resistor_4_node, shifter_1_out, shifter_2_out, shifter_3_out, shifter_4_out, shifter_5_out,
       shifter_6_out;

  assign controlled_buffer_1_out = not_1_out ? gen_obst : 1'bz;  // Controlled_Buffer controlled_buffer_1
  Pull_Resistor pull_resistor_1 (.node(controlled_buffer_1_out));
  not not_1 (not_1_out, t_ff_1_q);
  Random #(.width(4)) random_1 (
    .clk(controlled_buffer_1_out), .next(controlled_buffer_1_out), .out(random_1_out));  // open: clr
  Divider #(.width(4)) divider_1 (.a(random_1_out), .b(speed), .rem(divider_1_rem));  // open: out, upper
  common_speed common_speed_1 (.clk(common_speed_1_clk), .speed(divider_1_rem));
  T_Flip_Flop t_ff_1 (
    .clk(common_speed_1_clk), .T(counter_1_carry), .Q(t_ff_1_q), .preset(controlled_buffer_1_out));  // open: Qn, reset, en
  Counter #(.width(4), .max('h9)) counter_1 (
    .count(t_ff_1_q), .Q(counter_1_q), .carry(counter_1_carry), .clk(common_speed_1_clk));  // open: load, D, clr
  not not_2 (not_2_out, pause);
  not not_3 (not_3_out, t_ff_1_q);
  Multiplexer #(.enable("false")) multiplexer_1 (.in0(1'b0), .in1(gen_obst), .out(multiplexer_1_out), .sel(not_3_out));
  Pull_Resistor pull_resistor_2 (.node(birds_clk));
  assign birds_clk = not_2_out ? common_speed_1_clk : 1'bz;  // Controlled_Buffer controlled_buffer_2
  Pull_Resistor pull_resistor_3 (.node(pull_resistor_3_node));
  Multiplexer #(.select(4), .width(32)) multiplexer_2 (
    .in0(bird_1_out_1), .in1(bird_1_out_2), .in2(bird_1_out_3), .in3(bird_1_out_4), .in4(bird_1_out_5),
    .in5(bird_1_out_6), .in6(bird_1_out_7), .in7(bird_1_out_8), .in8(bird_1_out_9),
    .out(pull_resistor_3_node), .sel(counter_1_q), .en(t_ff_1_q));  // open: in9, in10, in11, in12, in13, in14, in15
  Shifter #(.width(32)) shifter_1 (.in(pull_resistor_3_node), .\dist (5'b00100), .out(shifter_1_out));
  Shifter #(.width(32)) shifter_2 (.in(pull_resistor_3_node), .\dist (5'b00111), .out(shifter_2_out));
  Shifter #(.width(32)) shifter_3 (.in(pull_resistor_3_node), .\dist (5'b10000), .out(shifter_3_out));
  Random #(.width(2)) random_2 (.clk(multiplexer_1_out), .next(multiplexer_1_out), .out(random_2_out));  // open: clr
  bird bird_1 (
    .out_1(bird_1_out_1), .out_2(bird_1_out_2), .out_3(bird_1_out_3), .out_4(bird_1_out_4),
    .out_5(bird_1_out_5), .out_6(bird_1_out_6), .out_7(bird_1_out_7), .out_8(bird_1_out_8),
    .out_9(bird_1_out_9), .out_10(bird_1_out_10), .out_11(bird_1_out_11), .out_12(bird_1_out_12),
    .out_13(bird_1_out_13), .out_14(bird_1_out_14), .out_15(bird_1_out_15), .out_16(bird_1_out_16),
    .out_17(bird_1_out_17), .out_18(bird_1_out_18));
  Multiplexer #(.select(2), .width(32), .enable("false")) multiplexer_3 (
    .in0(pull_resistor_3_node), .in1(shifter_1_out), .in2(shifter_2_out), .in3(shifter_3_out), .out(up),
    .sel(random_2_out));
  Pull_Resistor pull_resistor_4 (.node(pull_resistor_4_node));
  Multiplexer #(.select(4), .width(32)) multiplexer_4 (
    .in0(bird_1_out_10), .in1(bird_1_out_11), .in2(bird_1_out_12), .in3(bird_1_out_13), .in4(bird_1_out_14),
    .in5(bird_1_out_15), .in6(bird_1_out_16), .in7(bird_1_out_17), .in8(bird_1_out_18),
    .out(pull_resistor_4_node), .sel(counter_1_q), .en(t_ff_1_q));  // open: in9, in10, in11, in12, in13, in14, in15
  Shifter #(.width(32)) shifter_4 (.in(pull_resistor_4_node), .\dist (5'b00100), .out(shifter_4_out));
  Shifter #(.width(32)) shifter_5 (.in(pull_resistor_4_node), .\dist (5'b00111), .out(shifter_5_out));
  Shifter #(.width(32)) shifter_6 (.in(pull_resistor_4_node), .\dist (5'b10000), .out(shifter_6_out));
  Multiplexer #(.select(2), .width(32), .enable("false")) multiplexer_5 (
    .in0(pull_resistor_4_node), .in1(shifter_4_out), .in2(shifter_5_out), .in3(shifter_6_out), .out(down),
    .sel(random_2_out));
endmodule
