// Logisim project GoogleDino_cactus.circ as structural Verilog: 6 circuits, main circuit cacktus_test
module cacktus_test (
  input  \вывод ,
  input  \вывод_2 ,
  input  \тики ,
  input  \вывод_3 ,
  input  \тест ,
  input  \тики_2 ,
  input  \тики_3 ,
  input  \тест_2 ,
  input  \тест_3 ,
  input  \вывод_4 ,
  input  \тики_4 ,
  input  in_12,
  output [31:0] out_13,
  output [31:0] out_14,
  output [31:0] out_15,
  output [31:0] out_16,
  output \конец_вывода ,
  output \конец_вывода_2 ,
  output \конец_вывода_3 ,
  output \конец_вывода_4 
);

  wire and_1_out, and_2_out, and_3_out, and_4_out, button_1_out, button_2_out, clock_1_out, clock_2_out,
       clock_3_out, clock_4_out, or_1_out, or_2_out, or_3_out, or_4_out;
  wire [1:0] counter_3_q;
  wire [2:0] counter_2_q, counter_4_q, counter_5_q;
  wire [31:0] counter_1_q;

  DotMatrix #(.matrixcols(1), .matrixrows(32)) dotmatrix_1 (.col0(counter_1_q));
  // Probe on counter_1_q
  Counter #(.width(32), .max('hffffffff)) counter_1 (
    .Q(counter_1_q), .clk(button_1_out), .clr(button_2_out));  // open: load, D, count, carry
  Button button_1 (.out(button_1_out));
  Button button_2 (.out(button_2_out));
  DotMatrix #(.matrixrows(32)) dotmatrix_2 (.col0(32'h6), .col1(32'h2), .col2(32'h3f), .col3(32'h8), .col4(32'h78));
  Clock clock_1 (.out(clock_1_out));
  and and_1 (and_1_out, clock_1_out, \тест_2 );
  Multiplexer #(.select(3), .width(32)) multiplexer_1 (
    .in0(32'h6), .in1(32'h2), .in2(32'h3f), .in3(32'h8), .in4(32'h78), .out(out_14), .sel(counter_2_q));  // open: in5, in6, in7, en
  Counter #(.width(3), .max('h4)) counter_2 (
    .count(\вывод_2 ), .Q(counter_2_q), .carry(\конец_вывода_2 ), .clk(or_1_out));  // open: load, D, clr
  or or_1 (or_1_out, and_1_out, \тики_2 );
  DotMatrix #(.matrixcols(1), .matrixrows(32)) dotmatrix_3 (.col0(out_14));
  DotMatrix #(.matrixcols(3), .matrixrows(32)) dotmatrix_4 (.col0(32'h18), .col1(32'hf), .col2(32'h7a));
  or or_2 (or_2_out, and_2_out, \тики );
  Clock clock_2 (.out(clock_2_out));
  and and_2 (and_2_out, clock_2_out, \тест );
  DotMatrix #(.matrixcols(1), .matrixrows(32)) dotmatrix_5 (.col0(out_13));
  Multiplexer #(.select(2), .width(32)) multiplexer_2 (
    .in0(32'h18), .in1(32'hf), .in2(32'h7a), .out(out_13), .sel(counter_3_q));  // open: in3, en
  Counter #(.width(2), .max('h2)) counter_3 (
    .count(\вывод ), .Q(counter_3_q), .carry(\конец_вывода ), .clk(or_2_out));  // open: load, D, clr
  DotMatrix #(.matrixrows(32)) dotmatrix_6 (.col0(32'h7), .col1(32'h1), .col2(32'h7), .col3(32'h2), .col4(32'he));
  Clock clock_3 (.out(clock_3_out));
  Counter #(.width(3), .max('h4)) counter_4 (
    .count(\вывод_3 ), .Q(counter_4_q), .carry(\конец_вывода_3 ), .clk(or_3_out));  // open: load, D, clr
  or or_3 (or_3_out, and_3_out, \тики_3 );
  and and_3 (and_3_out, clock_3_out, \тест_3 );
  DotMatrix #(.matrixcols(1), .matrixrows(32)) dotmatrix_7 (.col0(out_15));
  Multiplexer #(.select(3), .width(32)) multiplexer_3 (
    .in0(32'h7), .in1(32'h1), .in2(32'h7), .in3(32'h2), .in4(32'he), .out(out_15), .sel(counter_4_q));  // open: in5, in6, in7, en
  DotMatrix #(.matrixcols(7), .matrixrows(32)) dotmatrix_8 (
    .col0(32'hc), .col1(32'h7), .col2(32'h3c), .col3({32{1'b0}}), .col4(32'h1c), .col5(32'h7), .col6(32'h1a));
  Clock clock_4 (.out(clock_4_out));
  Counter #(.width(3), .max('h6)) counter_5 (
    .count(\вывод_4 ), .Q(counter_5_q), .carry(\конец_вывода_4 ), .clk(or_4_out));  // open: load, D, clr
  or or_4 (or_4_out, and_4_out, \тики_4 );
  and and_4 (and_4_out, clock_4_out, in_12);
  DotMatrix #(.matrixcols(1), .matrixrows(32)) dotmatrix_9 (.col0(out_16));
  Multiplexer #(.select(3), .width(32)) multiplexer_4 (
    .in0(32'hc), .in1(32'h7), .in2(32'h3c), .in3({32{1'b0}}), .in4(32'h1c), .in5(32'h7), .in6(32'h1a),
    .out(out_16), .sel(counter_5_q));  // open: in7, en
endmodule

module obstacles (
  input  clk,
  input  get_obst,
  output [31:0] out
);

  wire \big_cactus_1_конец_вывода , \cacktus_1_конец_вывода , demultiplexer_1_out0, demultiplexer_1_out1,
       demultiplexer_1_out2, demultiplexer_1_out3, not_1_out, or_1_out, or_2_out, or_3_out, or_4_out,
       pull_resistor_1_node, \small_cactus_1_конец_вывода , t_ff_1_q, \wide_cactus_1_конец_вывода ;
  wire [3:0] divider_1_rem, random_1_out;
  wire [31:0] big_cactus_1_out_3, cacktus_1_out_3, small_cactus_1_out_3, wide_cactus_1_out_3;

  Pull_Resistor pull_resistor_1 (.node(pull_resistor_1_node));
  assign pull_resistor_1_node = not_1_out ? get_obst : 1'bz;  // Controlled_Buffer controlled_buffer_1
  not not_1 (not_1_out, t_ff_1_q);
  Random #(.width(4)) random_1 (
    .clk(pull_resistor_1_node), .next(pull_resistor_1_node), .out(random_1_out));  // open: clr
  or or_1 (or_1_out, pull_resistor_1_node, or_4_out);
  Divider #(.width(4)) divider_1 (.a(random_1_out), .b(4'b0100), .rem(divider_1_rem));  // open: out, upper
  T_Flip_Flop t_ff_1 (.clk(clk), .T(or_1_out), .Q(t_ff_1_q));  // open: Qn, preset, reset, en
  Demultiplexer #(.select(2), .disabled(0)) demultiplexer_1 (
    .out0(demultiplexer_1_out0), .out1(demultiplexer_1_out1), .out2(demultiplexer_1_out2),
    .out3(demultiplexer_1_out3), .in(1'b1), .sel(divider_1_rem[1:0]), .en(t_ff_1_q));
  cacktus cacktus_1 (
    .\вывод (demultiplexer_1_out0), .out_3(cacktus_1_out_3), .\конец_вывода (\cacktus_1_конец_вывода ),
    .\тики (clk));
  small_cactus small_cactus_1 (
    .\вывод (demultiplexer_1_out1), .out_3(small_cactus_1_out_3),
    .\конец_вывода (\small_cactus_1_конец_вывода ), .\тики (clk));
  or or_2 (or_2_out, \small_cactus_1_конец_вывода , \cacktus_1_конец_вывода );
  big_cactus big_cactus_1 (
    .\вывод (demultiplexer_1_out2), .out_3(big_cactus_1_out_3), .\конец_вывода (\big_cactus_1_конец_вывода ),
    .\тики (clk));
  or or_3 (or_3_out, \big_cactus_1_конец_вывода , or_2_out);
  wide_cactus wide_cactus_1 (
    .\вывод (demultiplexer_1_out3), .out_3(wide_cactus_1_out_3),
    .\конец_вывода (\wide_cactus_1_конец_вывода ), .\тики (clk));
  or or_4 (or_4_out, \wide_cactus_1_конец_вывода , or_3_out);
  Multiplexer #(.select(2), .width(32), .disabled(0)) multiplexer_1 (
    .in0(cacktus_1_out_3), .in1(small_cactus_1_out_3), .in2(big_cactus_1_out_3), .in3(wide_cactus_1_out_3),
    .out(out), .sel(divider_1_rem[1:0]), .en(t_ff_1_q));
endmodule

module big_cactus (
  input  \вывод ,
  input  \тики ,
  output [31:0] out_3,
  output \конец_вывода 
);

  wire [2:0] counter_1_q;

  DotMatrix #(.matrixrows(32)) dotmatrix_1 (.col0(32'h6), .col1(32'h2), .col2(32'h3f), .col3(32'h8), .col4(32'h78));
  Multiplexer #(.select(3), .width(32)) multiplexer_1 (
    .in0(32'h6), .in1(32'h2), .in2(32'h3f), .in3(32'h8), .in4(32'h78), .out(out_3), .sel(counter_1_q));  // open: in5, in6, in7, en
  Counter #(.width(3), .max('h4)) counter_1 (
    .count(\вывод ), .Q(counter_1_q), .carry(\конец_вывода ), .clk(\тики ));  // open: load, D, clr
  DotMatrix #(.matrixcols(1), .matrixrows(32)) dotmatrix_2 (.col0(out_3));
endmodule

module cacktus (
  input  \вывод ,
  input  \тики ,
  output [31:0] out_3,
  output \конец_вывода 
);

  wire [1:0] counter_1_q;

  DotMatrix #(.matrixcols(3), .matrixrows(32)) dotmatrix_1 (.col0(32'h7a), .col1(32'hf), .col2(32'h18));
  DotMatrix #(.matrixcols(1), .matrixrows(32)) dotmatrix_2 (.col0(out_3));
  Multiplexer #(.select(2), .width(32)) multiplexer_1 (
    .in0(32'h7a), .in1(32'hf), .in2(32'h18), .out(out_3), .sel(counter_1_q));  // open: in3, en
  Counter #(.width(2), .max('h2)) counter_1 (
    .count(\вывод ), .Q(counter_1_q), .carry(\конец_вывода ), .clk(\тики ));  // open: load, D, clr
endmodule

module wide_cactus (
  input  \вывод ,
  input  \тики ,
  output [31:0] out_3,
  output \конец_вывода 
);

  wire [2:0] counter_1_q;

  DotMatrix #(.matrixcols(7), .matrixrows(32)) dotmatrix_1 (
    .col0(32'hc), .col1(32'h7), .col2(32'h3c), .col3({32{1'b0}}), .col4(32'h1c), .col5(32'h7), .col6(32'h1a));
  Counter #(.width(3), .max('h6)) counter_1 (
    .count(\вывод ), .Q(counter_1_q), .carry(\конец_вывода ), .clk(\тики ));  // open: load, D, clr
  DotMatrix #(.matrixcols(1), .matrixrows(32)) dotmatrix_2 (.col0(out_3));
  Multiplexer #(.select(3), .width(32)) multiplexer_1 (
    .in0(32'hc), .in1(32'h7), .in2(32'h3c), .in3({32{1'b0}}), .in4(32'h1c), .in5(32'h7), .in6(32'h1a),
    .out(out_3), .sel(counter_1_q));  // open: in7, en
endmodule

module small_cactus (
  input  \вывод ,
  input  \тики ,
  output [31:0] out_3,
  output \конец_вывода 
);

  wire [2:0] counter_1_q;

  DotMatrix #(.matrixrows(32)) dotmatrix_1 (.col0(32'h7), .col1(32'h1), .col2(32'h7), .col3(32'h2), .col4(32'he));
  Multiplexer #(.select(3), .width(32)) multiplexer_1 (
    .in0(32'h7), .in1(32'h1), .in2(32'h7), .in3(32'h2), .in4(32'he), .out(out_3), .sel(counter_1_q));  // open: in5, in6, in7, en
  Counter #(.width(3), .max('h4)) counter_1 (
    .count(\вывод ), .Q(counter_1_q), .carry(\конец_вывода ), .clk(\тики ));  // open: load, D, clr
  DotMatrix #(.matrixcols(1), .matrixrows(32)) dotmatrix_2 (.col0(out_3));
endmodule
