// Logisim project GoogleDino_counter.circ as structural Verilog: 7 circuits, main circuit counter
module bcd_add (
  input  [3:0] A,
  input  [3:0] B,
  output [3:0] sum
);

  wire and_1_out, and_2_out, and_3_out, and_4_out, and_5_out, and_6_out, and_7_out, and_8_out, or_4_out,
       xor_1_out, xor_2_out, xor_3_out, xor_4_out, \с_2 , \с_3 , \с_4 ;

  xor xor_1 (xor_1_out, A[0], B[0]);
  and and_1 (and_1_out, A[0], B[0]);
  and and_2 (and_2_out, xor_1_out, 1'b0);
  xor xor_2 (xor_2_out, A[1], B[1]);
  and and_3 (and_3_out, A[1], B[1]);
  and and_4 (and_4_out, xor_2_out, \с_2 );
  xor xor_3 (xor_3_out, A[2], B[2]);
  and and_5 (and_5_out, A[2], B[2]);
  and and_6 (and_6_out, xor_3_out, \с_3 );
  xor xor_4 (xor_4_out, A[3], B[3]);
  and and_7 (and_7_out, A[3], B[3]);
  and and_8 (and_8_out, xor_4_out, \с_4 );
  xor xor_5 (sum[0], 1'b0, xor_1_out);
  or or_1 (\с_2 , and_1_out, and_2_out);
  xor xor_6 (sum[1], \с_2 , xor_2_out);
  or or_2 (\с_3 , and_3_out, and_4_out);
  xor xor_7 (sum[2], \с_3 , xor_3_out);
  or or_3 (\с_4 , and_5_out, and_6_out);
  xor xor_8 (sum[3], \с_4 , xor_4_out);
  or or_4 (or_4_out, and_7_out, and_8_out);
  // Probe on or_4_out
endmodule

module bcd_counter (
  input  clock,
  input  stop,
  input  reset,
  output [3:0] Out,
  output tens
);

  wire and_1_out, and_2_out, or_1_out;
  wire [3:0] bcd_add_1_sum, counter_1_q, register_1_q;

  and and_1 (and_1_out, clock, ~stop);  // AND_Gate
  and and_2 (and_2_out, and_1_out, ~reset);  // AND_Gate
  or or_1 (or_1_out, counter_1_q[3], counter_1_q[2], counter_1_q[1], counter_1_q[0]);
  Counter #(.width(4), .max('h9)) counter_1 (
    .load(1'b0), .count(1'b1), .Q(counter_1_q), .clk(and_2_out), .clr(reset));  // open: D, carry
  Register #(.width(4)) register_1 (.D(Out), .en(1'b1), .Q(register_1_q), .clk(and_2_out), .clr(1'b0));
  bcd_add bcd_add_1 (.A(register_1_q), .B(4'b0001), .sum(bcd_add_1_sum));
  Multiplexer #(.width(4)) multiplexer_1 (.in0(4'b0000), .in1(bcd_add_1_sum), .out(Out), .sel(or_1_out), .en(1'b1));
  Comparator #(.width(4)) comparator_1 (.a(4'b1001), .b(register_1_q), .eq(tens));  // open: gt, lt
endmodule

module counter (
  input  clock,
  input  stop,
  input  reset,
  output [3:0] _4,
  output [3:0] _3,
  output [3:0] _2,
  output [3:0] _1,
  output [3:0] hund,
  output [3:0] thous,
  output [15:0] out_10
);

  wire and_1_out, and_2_out, bcd_counter_1_tens, comparator_1_eq, comparator_2_eq, comparator_3_eq;

  and and_1 (and_1_out, clock, ~stop);  // AND_Gate
  and and_2 (and_2_out, and_1_out, ~reset);  // AND_Gate
  Counter #(.width(4), .max('h9)) counter_1 (
    .load(1'b0), .count(1'b1), .Q(_1), .clk(bcd_counter_1_tens), .clr(reset));  // open: D, carry
  bcd_counter bcd_counter_1 (.clock(and_2_out), .stop(stop), .tens(bcd_counter_1_tens), .reset(reset));  // open: Out
  Comparator #(.width(4)) comparator_1 (.a(4'b0000), .b(_1), .eq(comparator_1_eq));  // open: gt, lt
  Counter #(.width(4), .max('h9)) counter_2 (
    .load(1'b0), .count(1'b1), .Q(_2), .clk(comparator_1_eq), .clr(reset));  // open: D, carry
  Counter #(.width(4), .max('h9)) counter_3 (
    .load(1'b0), .count(1'b1), .Q(_3), .clk(comparator_2_eq), .clr(reset));  // open: D, carry
  Comparator #(.width(4)) comparator_2 (.a(4'b0000), .b(_2), .eq(comparator_2_eq));  // open: gt, lt
  Counter #(.width(4), .max('h9)) counter_4 (
    .load(1'b0), .count(1'b1), .Q(_4), .clk(comparator_3_eq), .clr(reset));  // open: D, carry
  Comparator #(.width(4)) comparator_3 (.a(4'b0000), .b(_3), .eq(comparator_3_eq));  // open: gt, lt

  assign hund = _2;
  assign out_10 = {_4, _3, _2, _1};
  assign thous = _3;
endmodule

module usage_example (
  input  in_1
);

  wire clock, reset;
  wire [3:0] counter_1__1, counter_1__2, counter_1__3, counter_1__4, hund, new_level_1_speed, thous;
  wire [5:0] new_level_1_out_5, new_level_1_out_6, new_level_1_out_7, new_level_1_out_8, new_level_1_out_9,
       new_level_1_out_10, new_level_1_out_11, new_level_1_out_12, new_level_1_out_13, new_level_1_out_14,
       new_level_1_out_15, new_level_1_out_16, new_level_1_out_17, new_level_1_out_19, new_level_1_out_20,
       new_level_1_out_21, new_level_1_out_22, new_level_1_out_23, new_level_1_out_24, new_level_1_out_25,
       new_level_1_out_26, new_level_1_out_27, new_level_1_out_28, new_level_1_out_29;

  Clock clock_1 (.out(clock));
  Button button_1 (.out(reset));
  new_level new_level_1 (
    .clock(clock), .hund(hund), .thous(thous), .reset(reset), .out_5(new_level_1_out_5),
    .out_6(new_level_1_out_6), .out_7(new_level_1_out_7), .out_8(new_level_1_out_8),
    .out_9(new_level_1_out_9), .out_10(new_level_1_out_10), .out_11(new_level_1_out_11),
    .out_12(new_level_1_out_12), .out_13(new_level_1_out_13), .out_14(new_level_1_out_14),
    .out_15(new_level_1_out_15), .out_16(new_level_1_out_16), .out_17(new_level_1_out_17),
    .speed(new_level_1_speed), .out_19(new_level_1_out_19), .out_20(new_level_1_out_20),
    .out_21(new_level_1_out_21), .out_22(new_level_1_out_22), .out_23(new_level_1_out_23),
    .out_24(new_level_1_out_24), .out_25(new_level_1_out_25), .out_26(new_level_1_out_26),
    .out_27(new_level_1_out_27), .out_28(new_level_1_out_28), .out_29(new_level_1_out_29));
  DotMatrix #(.matrixcols(24), .matrixrows(6)) dotmatrix_1 (
    .col0(new_level_1_out_5), .col1(new_level_1_out_6), .col2(new_level_1_out_10), .col3(new_level_1_out_11),
    .col4(new_level_1_out_12), .col5(new_level_1_out_13), .col6(new_level_1_out_14),
    .col7(new_level_1_out_15), .col8(new_level_1_out_16), .col9(new_level_1_out_17),
    .col10(new_level_1_out_19), .col11(new_level_1_out_20), .col12(new_level_1_out_21),
    .col13(new_level_1_out_22), .col14(new_level_1_out_23), .col15(new_level_1_out_24),
    .col16(new_level_1_out_25), .col17(new_level_1_out_26), .col18(new_level_1_out_27),
    .col19(new_level_1_out_28), .col20(new_level_1_out_29), .col21(new_level_1_out_7),
    .col22(new_level_1_out_8), .col23(new_level_1_out_9));
  Hex_Digit_Display hex_digit_display_1 (.value(counter_1__4));  // open: dp
  Hex_Digit_Display hex_digit_display_2 (.value(counter_1__3));  // open: dp
  Hex_Digit_Display hex_digit_display_3 (.value(counter_1__2));  // open: dp
  Hex_Digit_Display hex_digit_display_4 (.value(counter_1__1));  // open: dp
  counter counter_1 (
    .stop(in_1), .reset(reset), ._3(counter_1__3), ._2(counter_1__2), ._1(counter_1__1), .thous(thous),
    .clock(clock), .hund(hund), ._4(counter_1__4));  // open: out_10
  // Probe on new_level_1_speed

  // Other names for the same wires on the sheet: stop = in_1
endmodule

module new_level (
  input  clock,
  input  [3:0] hund,
  input  [3:0] thous,
  input  reset,
  output [5:0] out_5,
  output [5:0] out_6,
  output [5:0] out_7,
  output [5:0] out_8,
  output [5:0] out_9,
  output [5:0] out_10,
  output [5:0] out_11,
  output [5:0] out_12,
  output [5:0] out_13,
  output [5:0] out_14,
  output [5:0] out_15,
  output [5:0] out_16,
  output [5:0] out_17,
  output [3:0] speed,
  output [5:0] out_19,
  output [5:0] out_20,
  output [5:0] out_21,
  output [5:0] out_22,
  output [5:0] out_23,
  output [5:0] out_24,
  output [5:0] out_25,
  output [5:0] out_26,
  output [5:0] out_27,
  output [5:0] out_28,
  output [5:0] out_29
);

  wire cmp_1_out_5, comparator_1_eq, not_1_out;

  cmp cmp_1 (.hund(hund), .thous(thous), .reset(reset), .out_5(cmp_1_out_5), .clock(clock));
  not not_1 (not_1_out, comparator_1_eq);
  Multiplexer #(.select(3), .width(6), .enable("false")) multiplexer_1 (
    .in0(6'b010001), .in1(6'b110011), .in2(6'b100001), .in3(6'b111100), .in4(6'b111101), .out(out_7),
    .sel(speed[2:0]));  // open: in5, in6, in7
  Counter #(.width(4), .max('hf)) counter_1 (
    .load(1'b0), .count(not_1_out), .Q(speed), .clk(cmp_1_out_5), .clr(reset));  // open: D, carry
  Comparator #(.width(4)) comparator_1 (.a(speed), .b(4'b0101), .eq(comparator_1_eq));  // open: gt, lt
  Multiplexer #(.select(3), .width(6), .enable("false")) multiplexer_2 (
    .in0({6{1'b1}}), .in1(6'b100101), .in2(6'b100101), .in3(6'b000100), .in4(6'b100101), .out(out_8),
    .sel(speed[2:0]));  // open: in5, in6, in7
  // Probe on speed[3]
  Multiplexer #(.select(3), .width(6), .enable("false")) multiplexer_3 (
    .in0(6'b000001), .in1(6'b111001), .in2({6{1'b1}}), .in3({6{1'b1}}), .in4(6'b100111), .out(out_9),
    .sel(speed[2:0]));  // open: in5, in6, in7

  assign out_5 = {6{1'b1}};
  assign out_6 = 6'b000001;
  assign out_10 = 6'b000001;
  assign out_11 = {6{1'b0}};
  assign out_12 = {6{1'b1}};
  assign out_13 = 6'b101001;
  assign out_14 = 6'b101001;
  assign out_15 = {6{1'b0}};
  assign out_16 = 6'b111110;
  assign out_17 = 6'b000001;
  assign out_19 = 6'b111110;
  assign out_20 = {6{1'b0}};
  assign out_21 = {6{1'b1}};
  assign out_22 = 6'b101001;
  assign out_23 = 6'b101001;
  assign out_24 = {6{1'b0}};
  assign out_25 = {6{1'b1}};
  assign out_26 = 6'b000001;
  assign out_27 = 6'b000001;
  assign out_28 = {6{1'b0}};
  assign out_29 = {6{1'b0}};

  // Other names for the same wires on the sheet: clk = clock; clr = reset
endmodule

module cmp (
  input  clock,
  input  [3:0] hund,
  input  [3:0] thous,
  input  reset,
  output out_5
);

  wire and_1_out, and_2_out, and_3_out, and_4_out, and_5_out, and_6_out, and_7_out, comparator_1_eq,
       comparator_2_eq, comparator_3_eq, comparator_4_eq, comparator_5_eq, d_ff_1_q, d_ff_1_qn, d_ff_2_q,
       d_ff_2_qn, d_ff_3_qn, d_ff_4_qn;

  Comparator #(.width(4)) comparator_1 (.a(hund), .b(4'b0010), .eq(comparator_1_eq));  // open: gt, lt
  Comparator #(.width(4)) comparator_2 (.a(hund), .b(4'b1000), .eq(comparator_2_eq));  // open: gt, lt
  Comparator #(.width(4)) comparator_3 (.a(hund), .b(4'b0100), .eq(comparator_3_eq));  // open: gt, lt
  Comparator #(.width(4)) comparator_4 (.a(thous), .b(4'b0001), .eq(comparator_4_eq));  // open: gt, lt
  Comparator #(.width(4)) comparator_5 (.a(thous), .b(4'b0010), .eq(comparator_5_eq));  // open: gt, lt
  and and_1 (and_1_out, clock, ~d_ff_1_q);  // AND_Gate
  and and_2 (and_2_out, clock, ~d_ff_2_q);  // AND_Gate
  and and_3 (and_3_out, comparator_3_eq, comparator_4_eq);
  D_Flip_Flop #(.trigger("falling")) d_ff_1 (
    .clk(and_1_out), .D(comparator_1_eq), .Q(d_ff_1_q), .Qn(d_ff_1_qn), .reset(reset));  // open: preset, en
  D_Flip_Flop #(.trigger("falling")) d_ff_2 (
    .clk(and_2_out), .D(comparator_2_eq), .Q(d_ff_2_q), .Qn(d_ff_2_qn), .reset(reset));  // open: preset, en
  D_Flip_Flop #(.trigger("falling")) d_ff_3 (
    .clk(clock), .D(and_3_out), .Qn(d_ff_3_qn), .reset(reset));  // open: Q, preset, en
  D_Flip_Flop #(.trigger("falling")) d_ff_4 (
    .clk(clock), .D(comparator_5_eq), .Qn(d_ff_4_qn), .reset(reset));  // open: Q, preset, en
  and and_4 (and_4_out, d_ff_1_qn, comparator_1_eq, clock);
  and and_5 (and_5_out, d_ff_2_qn, comparator_2_eq, clock);
  and and_6 (and_6_out, d_ff_3_qn, and_3_out, clock);
  and and_7 (and_7_out, d_ff_4_qn, comparator_5_eq, clock);
  or or_1 (out_5, and_4_out, and_5_out, and_6_out, and_7_out);

  // Other names for the same wires on the sheet: clk = clock; clr = reset
endmodule

module number_sen (
  input  sen,
  input  reset,
  input  [15:0] num_in,
  output [7:0] num_out
);

  wire counter_1_q;

  Counter #(.width(1), .max('h1)) counter_1 (
    .load(1'b0), .count(1'b1), .Q(counter_1_q), .clk(sen), .clr(reset));  // open: D, carry
  Multiplexer #(.width(8), .enable("false")) multiplexer_1 (
    .in0(num_in[7:0]), .in1(num_in[15:8]), .out(num_out), .sel(counter_1_q));
endmodule
