// Logisim project GoogleDino_speed.circ as structural Verilog: 2 circuits, main circuit common_speed
module common_speed (
  input  [3:0] speed,
  output clk
);

  wire _1_out, _2_out, _3_out, _4_out, _5_out;

  Clock #(.lowDuration(6)) _1 (.out(_1_out));
  Clock #(.lowDuration(5)) _2 (.out(_2_out));
  Clock #(.lowDuration(4)) _3 (.out(_3_out));
  Clock _4 (.out(_4_out));
  Clock #(.lowDuration(2)) _5 (.out(_5_out));
  Multiplexer #(.select(4), .enable("false")) multiplexer_1 (
    .in0(_1_out), .in1(_2_out), .in2(_3_out), .in3(_4_out), .in4(_5_out), .out(clk), .sel(speed));  // open: in5, in6, in7, in8, in9, in10, in11, in12, in13, in14, in15

  // Notes on the sheet:
  //   level:
endmodule

module dino_speed (
  input  [3:0] speed,
  output clk
);

  wire _1_2_out, _3_5_out;

  Clock #(.lowDuration(20)) _1_2 (.out(_1_2_out));
  Clock #(.lowDuration(15)) _3_5 (.out(_3_5_out));
  Multiplexer #(.select(4), .enable("false")) multiplexer_1 (
    .in0(_1_2_out), .in1(_3_5_out), .out(clk), .sel(speed));  // open: in2, in3, in4, in5, in6, in7, in8, in9, in10, in11, in12, in13, in14, in15

  // Notes on the sheet:
  //   level:
endmodule
