// Logisim project GoogleDino_timer.circ as structural Verilog: 4 circuits, main circuit 10-counter
module _10_counter (
  input  clock_in,
  input  reset,
  output clock_out,
  output [3:0] out
);

  Counter #(.width(4), .max('h9)) counter_1 (
    .load(1'b0), .count(1'b1), .Q(out), .clk(clock_in), .clr(reset));  // open: D, carry
  and and_1 (clock_out, ~out[3], ~out[2], ~out[1], ~out[0]);  // AND_Gate
endmodule

module _6_counter (
  input  clock_in,
  input  reset,
  output clock_out,
  output [3:0] out
);

  wire comparator_1_gt, multiplexer_1_out;

  Counter #(.width(4), .max('hf)) counter_1 (
    .load(1'b0), .count(1'b1), .Q(out), .clk(clock_in), .clr(multiplexer_1_out));  // open: D, carry
  and and_1 (clock_out, ~out[2], ~out[1], ~out[0]);  // AND_Gate
  // Probe on out[3]
  Multiplexer multiplexer_1 (.in0(reset), .in1(1'b1), .out(multiplexer_1_out), .sel(comparator_1_gt), .en(1'b1));
  Comparator #(.width(4)) comparator_1 (.a(out), .b(4'b0101), .gt(comparator_1_gt));  // open: eq, lt
endmodule

module timer (
  input  clock,
  input  stop,
  input  reset,
  output [3:0] out_4,
  output [3:0] out_5,
  output out_6,
  output [3:0] out_7,
  output [3:0] out_8
);

  wire and_1_out, and_2_out, n6_counter_1_clock_out, n10_counter_1_clock_out, n10_counter_2_clock_out;

  and and_1 (and_1_out, clock, ~stop);  // AND_Gate
  and and_2 (and_2_out, and_1_out, ~reset);  // AND_Gate
  _10_counter u_10_counter_1 (
    .clock_in(n6_counter_1_clock_out), .reset(reset), .out(out_5), .clock_out(n10_counter_1_clock_out));
  _6_counter u_6_counter_1 (
    .clock_in(n10_counter_2_clock_out), .reset(reset), .out(out_7), .clock_out(n6_counter_1_clock_out));
  _10_counter u_10_counter_2 (.clock_in(and_2_out), .reset(reset), .out(out_8), .clock_out(n10_counter_2_clock_out));
  _6_counter u_6_counter_2 (.clock_in(n10_counter_1_clock_out), .reset(reset), .out(out_4));  // open: clock_out

  assign out_6 = 1'b1;

  // Other names for the same wires on the sheet: clr = reset
endmodule

module usage_example (
  input  in_1
);

  wire clock, reset, timer_1_out_6;
  wire [3:0] timer_1_out_4, timer_1_out_5, timer_1_out_7, timer_1_out_8;

  Button button_1 (.out(reset));
  Clock #(.highDuration(32), .lowDuration(32)) clock_1 (.out(clock));
  Hex_Digit_Display hex_digit_display_1 (.value(timer_1_out_4));  // open: dp
  Hex_Digit_Display hex_digit_display_2 (.value(timer_1_out_5), .dp(timer_1_out_6));
  timer timer_1 (
    .clock(clock), .stop(in_1), .out_4(timer_1_out_4), .out_5(timer_1_out_5), .out_6(timer_1_out_6),
    .out_7(timer_1_out_7), .out_8(timer_1_out_8), .reset(reset));
  Hex_Digit_Display hex_digit_display_3 (.value(timer_1_out_7));  // open: dp
  Hex_Digit_Display hex_digit_display_4 (.value(timer_1_out_8));  // open: dp

  // Other names for the same wires on the sheet: stop = in_1
endmodule
