// Logisim project cdm8.circ as structural Verilog: 4 circuits, main circuit main
module main (
  input  [7:0] char,
  input  [7:0] num,
  input  clock,
  input  ready,
  output [7:0] out_5,
  output clock_2,
  output sen_num,
  output sen_kboard
);

  wire and_1_out, and_2_out, and_3_out, and_4_out, cdm_8_1_p2, cdm_8_1_p3, cdm_8_1_p4, cdm_8_1_p5,
       cdm_8_1_p6, cdm_8_1_p7, cdm_8_1_p8, cdm_8_1_p9, cdm_8_1_p10, cdm_8_1_p11, comparator_1_eq,
       comparator_2_eq, decoder_1_out0, decoder_1_out1, nand_1_out, not_1_out, or_1_out, or_2_out;
  wire [7:0] cdm_8_1_p12, cdm_8_1_p13, cdm_8_1_p14;

  // Probe on cdm_8_1_p3
  // Probe on cdm_8_1_p2
  and and_1 (and_1_out, clock, nand_1_out);
  // Probe on cdm_8_1_p5
  // Probe on cdm_8_1_p4
  // Probe on cdm_8_1_p6
  nand nand_1 (nand_1_out, ~ready, or_1_out);  // NAND_Gate
  // Probe on cdm_8_1_p7
  // Probe on cdm_8_1_p8
  // CdM_8 cdm_8_1: pin names not known; wires that end beside it: and_1_out, cdm_8_1_p2, cdm_8_1_p3, cdm_8_1_p4, cdm_8_1_p5, cdm_8_1_p6, cdm_8_1_p7, cdm_8_1_p8, cdm_8_1_p9, cdm_8_1_p10, cdm_8_1_p11, cdm_8_1_p12, cdm_8_1_p13, cdm_8_1_p14
  not not_1 (not_1_out, cdm_8_1_p11);
  assign out_5 = not_1_out ? cdm_8_1_p13 : 8'bz;  // Controlled_Buffer controlled_buffer_1
  assign cdm_8_1_p14 = cdm_8_1_p11 ? out_5 : 8'bz;  // Controlled_Buffer controlled_buffer_2
  and and_2 (and_2_out, cdm_8_1_p11, decoder_1_out1, comparator_2_eq);
  or or_1 (or_1_out, and_2_out, and_3_out);
  Decoder #(.disabled(0)) decoder_1 (.out0(decoder_1_out0), .out1(decoder_1_out1), .sel(cdm_8_1_p9), .en(cdm_8_1_p10));
  assign out_5 = and_3_out ? char : 8'bz;  // Controlled_Buffer controlled_buffer_3
  and and_3 (and_3_out, cdm_8_1_p11, decoder_1_out1, comparator_1_eq);
  assign out_5 = and_2_out ? num : 8'bz;  // Controlled_Buffer controlled_buffer_4
  Pull_Resistor pull_resistor_1 (.node(cdm_8_1_p12));
  Comparator comparator_1 (.a(cdm_8_1_p12), .b({8{1'b1}}), .eq(comparator_1_eq));  // open: gt, lt
  Comparator comparator_2 (.a(cdm_8_1_p12), .b(8'hfe), .eq(comparator_2_eq));  // open: gt, lt
  D_Flip_Flop d_ff_1 (.clk(clock), .D(and_2_out), .Q(sen_num));  // open: Qn, preset, en, reset
  D_Flip_Flop d_ff_2 (.clk(clock), .D(and_3_out), .Q(sen_kboard));  // open: Qn, preset, en, reset
  ROM rom_1 (.addr(cdm_8_1_p12), .data(out_5), .sel(decoder_1_out0));
  RAM ram_1 (.addr(cdm_8_1_p12), .data(out_5), .sel(and_4_out), .clk(and_1_out), .ld(cdm_8_1_p11));  // open: clr
  and and_4 (and_4_out, decoder_1_out1, ~or_2_out);  // AND_Gate
  or or_2 (or_2_out, comparator_1_eq, comparator_2_eq);
  and and_5 (clock_2, ~cdm_8_1_p11, comparator_1_eq);  // AND_Gate

  // Notes on the sheet:
  //   numout
  //   contents of rom_1 (hex, n*v repeats v):
  //   cd fe d1 5 89 e0 d d0 ff b0 c0 ee 4 d1 3 89 e0 18 d0 fe b0 c0 ee f d0 5 b1 d2 5 76 e2 27 cb 0 3a 16
  //   ab 8d a1 d2 1 76 e1 3c d3 7 c8 0 8b e0 3a b1 d2 ff a9 8c ee 30 ee 2 d3 8 3a ae d3 6 3a ae d2 5 76 e8
  //   ff d3 5 bf 8b e0 b7 d2 6 b9 77 e2 b1 d0 7 a3 30 14 b0 8c b0 d2 1 16 ba 8e ba 72 e9 80 30 14 b0 d2 1
  //   16 ba b d2 1 16 a8 d0 0 14 a3 d2 6 b9 8d a9 d3 7 bf ee af e3 aa d0 0 14 b0 b0 d2 1 16 ba ba 72 e9 aa
  //   d0 0 14 b0 d2 1 16 ba b d2 1 16 a8 d0 0 14 a3 d2 6 b9 8d a9 d3 7 bf ee af d2 6 b9 8d a9 ee 4f d2 6
  //   35 a9 ee 4c d3 5 bf 8f d0 0 b0 8b e0 e5 d1 7 d2 7 a6 d1 7 b6 8a e0 d4 a6 b1 d2 ff a9 8c ee c6 d1 8
  //   b6 d0 5 b0 78 e2 e3 8e a6 d0 0 18 b0 ee be d3 5 bf d2 5 7b e1 fd cd e0 d0 e0 d1 0 b5 34 88 e0 fb c7
  //   ee f5 cc 7 ee 2 d4
  //   counter
  //   get
endmodule

module digit_output (
  input  [7:0] in_1,
  output [4:0] _1,
  output [4:0] _2,
  output [4:0] _3,
  output [4:0] _4,
  output [4:0] _5,
  output [4:0] _6,
  output [4:0] _7
);

  Multiplexer #(.select(4), .width(5), .enable("false")) multiplexer_1 (
    .in0({5{1'b1}}), .in1(5'b01001), .in2(5'b10111), .in3(5'b10101), .in4(5'b11100), .in5(5'b11101),
    .in6({5{1'b1}}), .in7(5'b10000), .in8({5{1'b1}}), .in9(5'b11101), .in10({5{1'b1}}), .out(_1),
    .sel(in_1[7:4]));  // open: in11, in12, in13, in14, in15
  Multiplexer #(.select(4), .width(5), .enable("false")) multiplexer_2 (
    .in0({5{1'b1}}), .in1(5'b01001), .in2(5'b10111), .in3(5'b10101), .in4(5'b11100), .in5(5'b11101),
    .in6({5{1'b1}}), .in7(5'b10000), .in8({5{1'b1}}), .in9(5'b11101), .in10({5{1'b1}}), .out(_5),
    .sel(in_1[3:0]));  // open: in11, in12, in13, in14, in15
  Multiplexer #(.select(4), .width(5), .enable("false")) multiplexer_3 (
    .in0(5'b10001), .in1({5{1'b1}}), .in2(5'b10101), .in3(5'b10101), .in4(5'b00100), .in5(5'b10101),
    .in6(5'b10101), .in7(5'b10000), .in8(5'b10101), .in9(5'b10101), .in10({5{1'b1}}), .out(_2),
    .sel(in_1[7:4]));  // open: in11, in12, in13, in14, in15
  Multiplexer #(.select(4), .width(5), .enable("false")) multiplexer_4 (
    .in0(5'b10001), .in1({5{1'b1}}), .in2(5'b10101), .in3(5'b10101), .in4(5'b00100), .in5(5'b10101),
    .in6(5'b10101), .in7(5'b10000), .in8(5'b10101), .in9(5'b10101), .in10({5{1'b1}}), .out(_6),
    .sel(in_1[3:0]));  // open: in11, in12, in13, in14, in15
  Multiplexer #(.select(4), .width(5), .enable("false")) multiplexer_5 (
    .in0({5{1'b1}}), .in1(5'b00001), .in2(5'b11101), .in3({5{1'b1}}), .in4({5{1'b1}}), .in5(5'b10111),
    .in6(5'b10111), .in7({5{1'b1}}), .in8({5{1'b1}}), .in9({5{1'b1}}), .in10({5{1'b1}}), .out(_3),
    .sel(in_1[7:4]));  // open: in11, in12, in13, in14, in15
  Multiplexer #(.select(4), .width(5), .enable("false")) multiplexer_6 (
    .in0({5{1'b1}}), .in1(5'b00001), .in2(5'b11101), .in3({5{1'b1}}), .in4({5{1'b1}}), .in5(5'b10111),
    .in6(5'b10111), .in7({5{1'b1}}), .in8({5{1'b1}}), .in9({5{1'b1}}), .in10({5{1'b1}}), .out(_7),
    .sel(in_1[3:0]));  // open: in11, in12, in13, in14, in15

  assign _4 = {5{1'b0}};
endmodule

module score_handler (
  input  [7:0] in_1,
  input  clock,
  input  reset,
  output [4:0] out_4,
  output [4:0] out_5,
  output [4:0] out_6,
  output [4:0] out_7,
  output [4:0] out_8,
  output [4:0] out_9,
  output [4:0] out_10,
  output [4:0] out_11,
  output [4:0] out_12,
  output [4:0] out_13,
  output [4:0] out_14,
  output [4:0] out_15,
  output [4:0] out_16,
  output [4:0] out_17,
  output [4:0] out_18,
  output [4:0] out_19,
  output [4:0] out_20,
  output [4:0] out_21,
  output [4:0] out_22,
  output [4:0] out_23,
  output [4:0] out_24,
  output [4:0] out_25,
  output [4:0] out_26,
  output [4:0] out_27,
  output [4:0] out_28,
  output [4:0] out_29,
  output [4:0] out_30,
  output [4:0] out_31,
  output [4:0] out_32,
  output [4:0] out_33,
  output [4:0] out_34,
  output [4:0] out_35,
  output [4:0] out_36,
  output [4:0] out_37,
  output [4:0] out_38,
  output [4:0] out_39,
  output [4:0] out_40,
  output [4:0] out_41,
  output [4:0] out_42,
  output [4:0] out_43,
  output [4:0] out_44,
  output [4:0] out_45,
  output [4:0] out_46,
  output [4:0] out_47,
  output [4:0] out_48,
  output [4:0] out_49,
  output [4:0] out_50,
  output [4:0] out_51,
  output [4:0] out_52,
  output [4:0] out_53,
  output [4:0] out_54,
  output [4:0] out_55,
  output [4:0] out_56,
  output [4:0] out_57,
  output [4:0] out_58,
  output [4:0] out_59,
  output [4:0] out_60,
  output [4:0] out_61,
  output [4:0] out_62,
  output [4:0] out_63,
  output [4:0] out_64,
  output [4:0] out_65,
  output [4:0] out_66,
  output [4:0] out_67,
  output [4:0] out_68,
  output [4:0] out_69,
  output [4:0] out_70,
  output [4:0] out_71,
  output [4:0] out_72,
  output [4:0] out_73,
  output [4:0] out_74,
  output [4:0] out_75,
  output [4:0] out_76,
  output [4:0] out_77,
  output [4:0] out_78,
  output [4:0] out_79,
  output [4:0] out_80,
  output [4:0] out_81,
  output [4:0] out_82,
  output [4:0] out_83,
  output [4:0] out_84,
  output [4:0] out_85,
  output [4:0] out_86,
  output [4:0] out_87,
  output [4:0] out_88,
  output [4:0] out_89,
  output [4:0] out_90,
  output [4:0] out_91,
  output [4:0] out_92,
  output [4:0] out_93,
  output [4:0] out_94,
  output [4:0] out_95,
  output [4:0] out_96,
  output [4:0] out_97,
  output [4:0] out_98,
  output [4:0] out_99,
  output [4:0] out_100,
  output [4:0] out_101,
  output [4:0] out_102,
  output [4:0] out_103,
  output [4:0] out_104,
  output [4:0] out_105,
  output [4:0] out_106,
  output [4:0] out_107,
  output [4:0] out_108,
  output [4:0] out_109,
  output [4:0] out_110,
  output [4:0] out_111,
  output [4:0] out_112,
  output [4:0] out_113,
  output [4:0] out_114,
  output [4:0] out_115,
  output [4:0] out_116,
  output [4:0] out_117,
  output [4:0] out_118,
  output [4:0] out_119,
  output [4:0] out_120,
  output [4:0] out_121,
  output [4:0] out_122,
  output [4:0] out_123,
  output [4:0] out_124,
  output [4:0] out_125,
  output [4:0] out_126,
  output [4:0] out_127,
  output [4:0] out_128,
  output [4:0] out_129,
  output [4:0] out_130,
  output [4:0] out_131,
  output [4:0] out_132,
  output [4:0] out_133,
  output [4:0] out_134,
  output [4:0] out_135,
  output [4:0] out_136,
  output [4:0] out_137,
  output [4:0] out_138,
  output [4:0] out_139,
  output [4:0] out_140,
  output [4:0] out_141,
  output [4:0] out_142,
  output [4:0] out_143,
  output [4:0] out_144,
  output [4:0] out_145,
  output [4:0] out_146,
  output [4:0] out_147,
  output [4:0] out_148,
  output [4:0] out_149,
  output [4:0] out_150,
  output [4:0] out_151,
  output [4:0] out_152,
  output [4:0] out_153,
  output [4:0] out_154,
  output [4:0] out_155,
  output [4:0] out_156,
  output [4:0] out_157,
  output [4:0] out_158
);

  wire and_1_out, and_2_out, and_3_out, and_4_out, and_5_out, and_6_out, and_7_out, and_8_out, and_9_out,
       and_10_out, and_11_out, and_12_out, and_13_out, and_14_out, and_15_out, and_16_out, and_17_out,
       and_18_out, and_19_out, and_20_out, and_21_out, and_22_out, and_23_out, and_24_out, and_25_out,
       and_26_out, and_27_out, and_28_out, and_29_out, and_30_out, and_31_out, comparator_1_gt,
       decoder_1_out0, decoder_1_out1, decoder_1_out2, decoder_1_out3, decoder_1_out4, decoder_2_out0,
       decoder_2_out1, decoder_2_out2, decoder_2_out3, decoder_2_out4, decoder_2_out5, multiplexer_1_out;
  wire [2:0] counter_1_q, counter_2_q;
  wire [7:0] _00, _01, _02, _03, _04, _05, _10, _11, _12, _13, _14, _15, _20, _21, _22, _23, _24, _25, _30,
       _31, _32, _33, _34, _35, _40, _41, _42, _43, _44, _45;

  Decoder #(.select(3), .enable("false")) decoder_1 (
    .out0(decoder_1_out0), .out1(decoder_1_out1), .out2(decoder_1_out2), .out3(decoder_1_out3),
    .out4(decoder_1_out4), .sel(counter_1_q));  // open: out5, out6, out7
  Counter #(.width(3), .max('h7)) counter_1 (
    .load(1'b0), .count(1'b1), .Q(counter_1_q), .clk(and_6_out), .clr(reset));  // open: D, carry
  symbol_output symbol_output_1 (.in_1(_05), .out_2(out_4), .out_3(out_5), .out_4(out_6));
  symbol_output symbol_output_2 (.in_1(_15), .out_2(out_35), .out_3(out_36), .out_4(out_37));
  symbol_output symbol_output_3 (.in_1(_25), .out_2(out_66), .out_3(out_67), .out_4(out_68));
  symbol_output symbol_output_4 (.in_1(_35), .out_2(out_97), .out_3(out_98), .out_4(out_99));
  symbol_output symbol_output_5 (.in_1(_45), .out_2(out_128), .out_3(out_129), .out_4(out_130));
  and and_1 (and_1_out, decoder_1_out0, decoder_2_out5);
  and and_2 (and_2_out, decoder_1_out1, decoder_2_out5);
  and and_3 (and_3_out, decoder_1_out2, decoder_2_out5);
  and and_4 (and_4_out, decoder_1_out3, decoder_2_out5);
  and and_5 (and_5_out, decoder_1_out4, decoder_2_out5);
  Decoder #(.select(3), .enable("false")) decoder_2 (
    .out0(decoder_2_out0), .out1(decoder_2_out1), .out2(decoder_2_out2), .out3(decoder_2_out3),
    .out4(decoder_2_out4), .out5(decoder_2_out5), .sel(counter_2_q));  // open: out6, out7
  symbol_output symbol_output_6 (.in_1(_04), .out_2(out_8), .out_3(out_9), .out_4(out_10));
  symbol_output symbol_output_7 (.in_1(_14), .out_2(out_39), .out_3(out_40), .out_4(out_41));
  symbol_output symbol_output_8 (.in_1(_24), .out_2(out_70), .out_3(out_71), .out_4(out_72));
  symbol_output symbol_output_9 (.in_1(_34), .out_2(out_101), .out_3(out_102), .out_4(out_103));
  symbol_output symbol_output_10 (.in_1(_44), .out_2(out_132), .out_3(out_133), .out_4(out_134));
  Register register_1 (.D(in_1), .en(and_1_out), .Q(_05), .clk(clock), .clr(reset));
  Register register_2 (.D(in_1), .en(and_2_out), .Q(_15), .clk(clock), .clr(reset));
  Register register_3 (.D(in_1), .en(and_3_out), .Q(_25), .clk(clock), .clr(reset));
  Register register_4 (.D(in_1), .en(and_4_out), .Q(_35), .clk(clock), .clr(reset));
  Register register_5 (.D(in_1), .en(and_5_out), .Q(_45), .clk(clock), .clr(reset));
  and and_6 (and_6_out, ~counter_2_q[2], ~counter_2_q[1], ~counter_2_q[0]);  // AND_Gate
  Counter #(.width(3), .max('h7)) counter_2 (
    .load(1'b0), .count(1'b1), .Q(counter_2_q), .clk(clock), .clr(multiplexer_1_out));  // open: D, carry
  and and_7 (and_7_out, decoder_1_out0, decoder_2_out4);
  and and_8 (and_8_out, decoder_1_out1, decoder_2_out4);
  and and_9 (and_9_out, decoder_1_out2, decoder_2_out4);
  and and_10 (and_10_out, decoder_1_out3, decoder_2_out4);
  and and_11 (and_11_out, decoder_1_out4, decoder_2_out4);
  Comparator #(.width(3), .mode("unsigned")) comparator_1 (
    .a(counter_2_q), .b(3'b101), .gt(comparator_1_gt));  // open: eq, lt
  Register register_6 (.D(in_1), .en(and_7_out), .Q(_04), .clk(clock), .clr(reset));
  Register register_7 (.D(in_1), .en(and_8_out), .Q(_14), .clk(clock), .clr(reset));
  Register register_8 (.D(in_1), .en(and_9_out), .Q(_24), .clk(clock), .clr(reset));
  Register register_9 (.D(in_1), .en(and_10_out), .Q(_34), .clk(clock), .clr(reset));
  Register register_10 (.D(in_1), .en(and_11_out), .Q(_44), .clk(clock), .clr(reset));
  Multiplexer multiplexer_1 (.in0(reset), .in1(1'b1), .out(multiplexer_1_out), .sel(comparator_1_gt), .en(1'b1));
  symbol_output symbol_output_11 (.in_1(_03), .out_2(out_12), .out_3(out_13), .out_4(out_14));
  symbol_output symbol_output_12 (.in_1(_13), .out_2(out_43), .out_3(out_44), .out_4(out_45));
  symbol_output symbol_output_13 (.in_1(_23), .out_2(out_74), .out_3(out_75), .out_4(out_76));
  symbol_output symbol_output_14 (.in_1(_33), .out_2(out_105), .out_3(out_106), .out_4(out_107));
  symbol_output symbol_output_15 (.in_1(_43), .out_2(out_136), .out_3(out_137), .out_4(out_138));
  Register register_11 (.D(in_1), .en(and_12_out), .Q(_03), .clk(clock), .clr(reset));
  and and_12 (and_12_out, decoder_1_out0, decoder_2_out3);
  Register register_12 (.D(in_1), .en(and_13_out), .Q(_13), .clk(clock), .clr(reset));
  and and_13 (and_13_out, decoder_1_out1, decoder_2_out3);
  Register register_13 (.D(in_1), .en(and_14_out), .Q(_23), .clk(clock), .clr(reset));
  and and_14 (and_14_out, decoder_1_out2, decoder_2_out3);
  Register register_14 (.D(in_1), .en(and_15_out), .Q(_33), .clk(clock), .clr(reset));
  and and_15 (and_15_out, decoder_1_out3, decoder_2_out3);
  Register register_15 (.D(in_1), .en(and_16_out), .Q(_43), .clk(clock), .clr(reset));
  and and_16 (and_16_out, decoder_1_out4, decoder_2_out3);
  symbol_output symbol_output_16 (.in_1(_02), .out_2(out_16), .out_3(out_17), .out_4(out_18));
  symbol_output symbol_output_17 (.in_1(_12), .out_2(out_47), .out_3(out_48), .out_4(out_49));
  symbol_output symbol_output_18 (.in_1(_22), .out_2(out_78), .out_3(out_79), .out_4(out_80));
  symbol_output symbol_output_19 (.in_1(_32), .out_2(out_109), .out_3(out_110), .out_4(out_111));
  symbol_output symbol_output_20 (.in_1(_42), .out_2(out_140), .out_3(out_141), .out_4(out_142));
  Register register_16 (.D(in_1), .en(and_17_out), .Q(_02), .clk(clock), .clr(reset));
  and and_17 (and_17_out, decoder_1_out0, decoder_2_out2);
  Register register_17 (.D(in_1), .en(and_18_out), .Q(_12), .clk(clock), .clr(reset));
  and and_18 (and_18_out, decoder_1_out1, decoder_2_out2);
  Register register_18 (.D(in_1), .en(and_19_out), .Q(_22), .clk(clock), .clr(reset));
  and and_19 (and_19_out, decoder_1_out2, decoder_2_out2);
  Register register_19 (.D(in_1), .en(and_20_out), .Q(_32), .clk(clock), .clr(reset));
  and and_20 (and_20_out, decoder_1_out3, decoder_2_out2);
  Register register_20 (.D(in_1), .en(and_21_out), .Q(_42), .clk(clock), .clr(reset));
  and and_21 (and_21_out, decoder_1_out4, decoder_2_out2);
  and and_22 (and_22_out, decoder_1_out0, decoder_2_out1);
  and and_23 (and_23_out, decoder_1_out1, decoder_2_out1);
  and and_24 (and_24_out, decoder_1_out2, decoder_2_out1);
  and and_25 (and_25_out, decoder_1_out3, decoder_2_out1);
  and and_26 (and_26_out, decoder_1_out4, decoder_2_out1);
  Register register_21 (.D(in_1), .en(and_22_out), .Q(_01), .clk(clock), .clr(reset));
  Register register_22 (.D(in_1), .en(and_23_out), .Q(_11), .clk(clock), .clr(reset));
  Register register_23 (.D(in_1), .en(and_24_out), .Q(_21), .clk(clock), .clr(reset));
  Register register_24 (.D(in_1), .en(and_25_out), .Q(_31), .clk(clock), .clr(reset));
  Register register_25 (.D(in_1), .en(and_26_out), .Q(_41), .clk(clock), .clr(reset));
  and and_27 (and_27_out, decoder_1_out0, decoder_2_out0);
  and and_28 (and_28_out, decoder_1_out1, decoder_2_out0);
  and and_29 (and_29_out, decoder_1_out2, decoder_2_out0);
  and and_30 (and_30_out, decoder_1_out3, decoder_2_out0);
  and and_31 (and_31_out, decoder_1_out4, decoder_2_out0);
  digit_output digit_output_1 (
    .in_1(_00), ._1(out_20), ._2(out_21), ._3(out_22), ._4(out_23), ._5(out_24), ._6(out_25), ._7(out_26));
  digit_output digit_output_2 (
    .in_1(_10), ._1(out_51), ._2(out_52), ._3(out_53), ._4(out_54), ._5(out_55), ._6(out_56), ._7(out_57));
  digit_output digit_output_3 (
    .in_1(_20), ._1(out_82), ._2(out_83), ._3(out_84), ._4(out_85), ._5(out_86), ._6(out_87), ._7(out_88));
  digit_output digit_output_4 (
    .in_1(_30), ._1(out_113), ._2(out_114), ._3(out_115), ._4(out_116), ._5(out_117), ._6(out_118),
    ._7(out_119));
  digit_output digit_output_5 (
    .in_1(_40), ._1(out_144), ._2(out_145), ._3(out_146), ._4(out_147), ._5(out_148), ._6(out_149),
    ._7(out_150));
  Register register_26 (.D(in_1), .en(and_27_out), .Q(_00), .clk(clock), .clr(reset));
  Register register_27 (.D(in_1), .en(and_28_out), .Q(_10), .clk(clock), .clr(reset));
  Register register_28 (.D(in_1), .en(and_29_out), .Q(_20), .clk(clock), .clr(reset));
  Register register_29 (.D(in_1), .en(and_30_out), .Q(_30), .clk(clock), .clr(reset));
  Register register_30 (.D(in_1), .en(and_31_out), .Q(_40), .clk(clock), .clr(reset));
  digit_output digit_output_6 (
    .in_1(_01), ._1(out_28), ._2(out_29), ._3(out_30), ._4(out_31), ._5(out_32), ._6(out_33), ._7(out_34));
  digit_output digit_output_7 (
    .in_1(_11), ._1(out_59), ._2(out_60), ._3(out_61), ._4(out_62), ._5(out_63), ._6(out_64), ._7(out_65));
  digit_output digit_output_8 (
    .in_1(_21), ._1(out_90), ._2(out_91), ._3(out_92), ._4(out_93), ._5(out_94), ._6(out_95), ._7(out_96));
  digit_output digit_output_9 (
    .in_1(_31), ._1(out_121), ._2(out_122), ._3(out_123), ._4(out_124), ._5(out_125), ._6(out_126),
    ._7(out_127));
  digit_output digit_output_10 (
    .in_1(_41), ._1(out_152), ._2(out_153), ._3(out_154), ._4(out_155), ._5(out_156), ._6(out_157),
    ._7(out_158));

  assign out_7 = {5{1'b0}};
  assign out_11 = {5{1'b0}};
  assign out_15 = {5{1'b0}};
  assign out_19 = {5{1'b0}};
  assign out_27 = {5{1'b0}};
  assign out_38 = {5{1'b0}};
  assign out_42 = {5{1'b0}};
  assign out_46 = {5{1'b0}};
  assign out_50 = {5{1'b0}};
  assign out_58 = {5{1'b0}};
  assign out_69 = {5{1'b0}};
  assign out_73 = {5{1'b0}};
  assign out_77 = {5{1'b0}};
  assign out_81 = {5{1'b0}};
  assign out_89 = {5{1'b0}};
  assign out_100 = {5{1'b0}};
  assign out_104 = {5{1'b0}};
  assign out_108 = {5{1'b0}};
  assign out_112 = {5{1'b0}};
  assign out_120 = {5{1'b0}};
  assign out_131 = {5{1'b0}};
  assign out_135 = {5{1'b0}};
  assign out_139 = {5{1'b0}};
  assign out_143 = {5{1'b0}};
  assign out_151 = {5{1'b0}};
endmodule

module symbol_output (
  input  [7:0] in_1,
  output [4:0] out_2,
  output [4:0] out_3,
  output [4:0] out_4
);

  wire comparator_1_eq, comparator_2_eq, comparator_3_eq, comparator_4_eq, comparator_5_eq, comparator_6_eq,
       comparator_7_eq, comparator_8_eq, comparator_9_eq, comparator_10_eq, comparator_11_eq,
       comparator_12_eq, comparator_13_eq, comparator_14_eq, comparator_15_eq, comparator_16_eq,
       comparator_17_eq, comparator_18_eq, comparator_19_eq, comparator_20_eq, comparator_21_eq,
       comparator_22_eq, comparator_23_eq, comparator_24_eq, comparator_25_eq, comparator_26_eq,
       comparator_27_eq;

  Pull_Resistor pull_resistor_1 (.node(out_2));
  assign out_2 = comparator_1_eq ? 5'b01111 : 5'bz;  // Controlled_Buffer controlled_buffer_1
  Comparator comparator_1 (.a(8'h61), .b(in_1), .eq(comparator_1_eq));  // open: gt, lt
  assign out_2 = comparator_2_eq ? {5{1'b1}} : 5'bz;  // Controlled_Buffer controlled_buffer_2
  Comparator comparator_2 (.a(8'h62), .b(in_1), .eq(comparator_2_eq));  // open: gt, lt
  assign out_2 = comparator_3_eq ? {5{1'b1}} : 5'bz;  // Controlled_Buffer controlled_buffer_3
  Comparator comparator_3 (.a(8'h63), .b(in_1), .eq(comparator_3_eq));  // open: gt, lt
  assign out_2 = comparator_4_eq ? {5{1'b1}} : 5'bz;  // Controlled_Buffer controlled_buffer_4
  Comparator comparator_4 (.a(8'h64), .b(in_1), .eq(comparator_4_eq));  // open: gt, lt
  assign out_2 = comparator_5_eq ? {5{1'b1}} : 5'bz;  // Controlled_Buffer controlled_buffer_5
  Comparator comparator_5 (.a(8'h65), .b(in_1), .eq(comparator_5_eq));  // open: gt, lt
  assign out_2 = comparator_6_eq ? {5{1'b1}} : 5'bz;  // Controlled_Buffer controlled_buffer_6
  Comparator comparator_6 (.a(8'h66), .b(in_1), .eq(comparator_6_eq));  // open: gt, lt
  assign out_2 = comparator_7_eq ? 5'b01111 : 5'bz;  // Controlled_Buffer controlled_buffer_7
  Comparator comparator_7 (.a(8'h67), .b(in_1), .eq(comparator_7_eq));  // open: gt, lt
  assign out_2 = comparator_8_eq ? {5{1'b1}} : 5'bz;  // Controlled_Buffer controlled_buffer_8
  Comparator comparator_8 (.a(8'h68), .b(in_1), .eq(comparator_8_eq));  // open: gt, lt
  assign out_2 = comparator_9_eq ? 5'b10001 : 5'bz;  // Controlled_Buffer controlled_buffer_9
  Comparator comparator_9 (.a(8'h69), .b(in_1), .eq(comparator_9_eq));  // open: gt, lt
  assign out_2 = comparator_10_eq ? 5'b10001 : 5'bz;  // Controlled_Buffer controlled_buffer_10
  Comparator comparator_10 (.a(8'h6a), .b(in_1), .eq(comparator_10_eq));  // open: gt, lt
  assign out_2 = comparator_11_eq ? {5{1'b1}} : 5'bz;  // Controlled_Buffer controlled_buffer_11
  Comparator comparator_11 (.a(8'h6b), .b(in_1), .eq(comparator_11_eq));  // open: gt, lt
  assign out_2 = comparator_12_eq ? {5{1'b1}} : 5'bz;  // Controlled_Buffer controlled_buffer_12
  Comparator comparator_12 (.a(8'h6c), .b(in_1), .eq(comparator_12_eq));  // open: gt, lt
  assign out_2 = comparator_13_eq ? {5{1'b1}} : 5'bz;  // Controlled_Buffer controlled_buffer_13
  Comparator comparator_13 (.a(8'h6d), .b(in_1), .eq(comparator_13_eq));  // open: gt, lt
  assign out_2 = comparator_14_eq ? 5'b01111 : 5'bz;  // Controlled_Buffer controlled_buffer_14
  Comparator comparator_14 (.a(8'h6e), .b(in_1), .eq(comparator_14_eq));  // open: gt, lt
  assign out_2 = comparator_15_eq ? {5{1'b1}} : 5'bz;  // Controlled_Buffer controlled_buffer_15
  Comparator comparator_15 (.a(8'h6f), .b(in_1), .eq(comparator_15_eq));  // open: gt, lt
  assign out_2 = comparator_16_eq ? {5{1'b1}} : 5'bz;  // Controlled_Buffer controlled_buffer_16
  Comparator comparator_16 (.a(8'h70), .b(in_1), .eq(comparator_16_eq));  // open: gt, lt
  assign out_2 = comparator_17_eq ? 5'b11110 : 5'bz;  // Controlled_Buffer controlled_buffer_17
  Comparator comparator_17 (.a(8'h71), .b(in_1), .eq(comparator_17_eq));  // open: gt, lt
  assign out_2 = comparator_18_eq ? {5{1'b1}} : 5'bz;  // Controlled_Buffer controlled_buffer_18
  Comparator comparator_18 (.a(8'h72), .b(in_1), .eq(comparator_18_eq));  // open: gt, lt
  assign out_2 = comparator_19_eq ? 5'b11101 : 5'bz;  // Controlled_Buffer controlled_buffer_19
  Comparator comparator_19 (.a(8'h73), .b(in_1), .eq(comparator_19_eq));  // open: gt, lt
  assign out_2 = comparator_20_eq ? 5'b10000 : 5'bz;  // Controlled_Buffer controlled_buffer_20
  Comparator comparator_20 (.a(8'h74), .b(in_1), .eq(comparator_20_eq));  // open: gt, lt
  assign out_2 = comparator_21_eq ? {5{1'b1}} : 5'bz;  // Controlled_Buffer controlled_buffer_21
  Comparator comparator_21 (.a(8'h75), .b(in_1), .eq(comparator_21_eq));  // open: gt, lt
  assign out_2 = comparator_22_eq ? 5'b11110 : 5'bz;  // Controlled_Buffer controlled_buffer_22
  Comparator comparator_22 (.a(8'h76), .b(in_1), .eq(comparator_22_eq));  // open: gt, lt
  assign out_2 = comparator_23_eq ? {5{1'b1}} : 5'bz;  // Controlled_Buffer controlled_buffer_23
  Comparator comparator_23 (.a(8'h77), .b(in_1), .eq(comparator_23_eq));  // open: gt, lt
  assign out_2 = comparator_24_eq ? 5'b11011 : 5'bz;  // Controlled_Buffer controlled_buffer_24
  Comparator comparator_24 (.a(8'h78), .b(in_1), .eq(comparator_24_eq));  // open: gt, lt
  assign out_2 = comparator_25_eq ? 5'b11000 : 5'bz;  // Controlled_Buffer controlled_buffer_25
  Comparator comparator_25 (.a(8'h79), .b(in_1), .eq(comparator_25_eq));  // open: gt, lt
  assign out_2 = comparator_26_eq ? 5'b10011 : 5'bz;  // Controlled_Buffer controlled_buffer_26
  Comparator comparator_26 (.a(8'h7a), .b(in_1), .eq(comparator_26_eq));  // open: gt, lt
  assign out_2 = comparator_27_eq ? {5{1'b0}} : 5'bz;  // Controlled_Buffer controlled_buffer_27
  Comparator comparator_27 (.a(8'hcd), .b(in_1), .eq(comparator_27_eq));  // open: gt, lt
  DotMatrix #(.matrixcols(3), .matrixrows(5)) dotmatrix_1 (.col0(out_2), .col1(out_3), .col2(out_4));
  Pull_Resistor pull_resistor_2 (.node(out_3));
  assign out_3 = comparator_1_eq ? 5'b10100 : 5'bz;  // Controlled_Buffer controlled_buffer_28
  assign out_3 = comparator_2_eq ? 5'b10101 : 5'bz;  // Controlled_Buffer controlled_buffer_29
  assign out_3 = comparator_3_eq ? 5'b10001 : 5'bz;  // Controlled_Buffer controlled_buffer_30
  assign out_3 = comparator_4_eq ? 5'b10001 : 5'bz;  // Controlled_Buffer controlled_buffer_31
  assign out_3 = comparator_5_eq ? 5'b10101 : 5'bz;  // Controlled_Buffer controlled_buffer_32
  assign out_3 = comparator_6_eq ? 5'b10100 : 5'bz;  // Controlled_Buffer controlled_buffer_33
  assign out_3 = comparator_7_eq ? 5'b10001 : 5'bz;  // Controlled_Buffer controlled_buffer_34
  assign out_3 = comparator_8_eq ? 5'b00100 : 5'bz;  // Controlled_Buffer controlled_buffer_35
  assign out_3 = comparator_9_eq ? {5{1'b1}} : 5'bz;  // Controlled_Buffer controlled_buffer_36
  assign out_3 = comparator_10_eq ? {5{1'b1}} : 5'bz;  // Controlled_Buffer controlled_buffer_37
  assign out_3 = comparator_11_eq ? 5'b00100 : 5'bz;  // Controlled_Buffer controlled_buffer_38
  assign out_3 = comparator_12_eq ? 5'b00001 : 5'bz;  // Controlled_Buffer controlled_buffer_39
  assign out_3 = comparator_13_eq ? 5'b01000 : 5'bz;  // Controlled_Buffer controlled_buffer_40
  assign out_3 = comparator_14_eq ? 5'b00100 : 5'bz;  // Controlled_Buffer controlled_buffer_41
  assign out_3 = comparator_15_eq ? 5'b10001 : 5'bz;  // Controlled_Buffer controlled_buffer_42
  assign out_3 = comparator_16_eq ? 5'b10100 : 5'bz;  // Controlled_Buffer controlled_buffer_43
  assign out_3 = comparator_17_eq ? 5'b10010 : 5'bz;  // Controlled_Buffer controlled_buffer_44
  assign out_3 = comparator_18_eq ? 5'b10100 : 5'bz;  // Controlled_Buffer controlled_buffer_45
  assign out_3 = comparator_19_eq ? 5'b10101 : 5'bz;  // Controlled_Buffer controlled_buffer_46
  assign out_3 = comparator_20_eq ? {5{1'b1}} : 5'bz;  // Controlled_Buffer controlled_buffer_47
  assign out_3 = comparator_21_eq ? 5'b00001 : 5'bz;  // Controlled_Buffer controlled_buffer_48
  assign out_3 = comparator_22_eq ? 5'b00001 : 5'bz;  // Controlled_Buffer controlled_buffer_49
  assign out_3 = comparator_23_eq ? 5'b00010 : 5'bz;  // Controlled_Buffer controlled_buffer_50
  assign out_3 = comparator_24_eq ? 5'b00100 : 5'bz;  // Controlled_Buffer controlled_buffer_51
  assign out_3 = comparator_25_eq ? 5'b00111 : 5'bz;  // Controlled_Buffer controlled_buffer_52
  assign out_3 = comparator_26_eq ? 5'b10101 : 5'bz;  // Controlled_Buffer controlled_buffer_53
  assign out_3 = comparator_27_eq ? {5{1'b0}} : 5'bz;  // Controlled_Buffer controlled_buffer_54
  Pull_Resistor pull_resistor_3 (.node(out_4));
  assign out_4 = comparator_1_eq ? 5'b01111 : 5'bz;  // Controlled_Buffer controlled_buffer_55
  assign out_4 = comparator_2_eq ? 5'b01010 : 5'bz;  // Controlled_Buffer controlled_buffer_56
  assign out_4 = comparator_3_eq ? 5'b10001 : 5'bz;  // Controlled_Buffer controlled_buffer_57
  assign out_4 = comparator_4_eq ? 5'b01110 : 5'bz;  // Controlled_Buffer controlled_buffer_58
  assign out_4 = comparator_5_eq ? 5'b10101 : 5'bz;  // Controlled_Buffer controlled_buffer_59
  assign out_4 = comparator_6_eq ? 5'b10100 : 5'bz;  // Controlled_Buffer controlled_buffer_60
  assign out_4 = comparator_7_eq ? 5'b10110 : 5'bz;  // Controlled_Buffer controlled_buffer_61
  assign out_4 = comparator_8_eq ? {5{1'b1}} : 5'bz;  // Controlled_Buffer controlled_buffer_62
  assign out_4 = comparator_9_eq ? 5'b10001 : 5'bz;  // Controlled_Buffer controlled_buffer_63
  assign out_4 = comparator_10_eq ? 5'b10000 : 5'bz;  // Controlled_Buffer controlled_buffer_64
  assign out_4 = comparator_11_eq ? 5'b11011 : 5'bz;  // Controlled_Buffer controlled_buffer_65
  assign out_4 = comparator_12_eq ? 5'b00001 : 5'bz;  // Controlled_Buffer controlled_buffer_66
  assign out_4 = comparator_13_eq ? {5{1'b1}} : 5'bz;  // Controlled_Buffer controlled_buffer_67
  assign out_4 = comparator_14_eq ? 5'b11110 : 5'bz;  // Controlled_Buffer controlled_buffer_68
  assign out_4 = comparator_15_eq ? {5{1'b1}} : 5'bz;  // Controlled_Buffer controlled_buffer_69
  assign out_4 = comparator_16_eq ? 5'b11100 : 5'bz;  // Controlled_Buffer controlled_buffer_70
  assign out_4 = comparator_17_eq ? 5'b11101 : 5'bz;  // Controlled_Buffer controlled_buffer_71
  assign out_4 = comparator_18_eq ? 5'b11011 : 5'bz;  // Controlled_Buffer controlled_buffer_72
  assign out_4 = comparator_19_eq ? 5'b10111 : 5'bz;  // Controlled_Buffer controlled_buffer_73
  assign out_4 = comparator_20_eq ? 5'b10000 : 5'bz;  // Controlled_Buffer controlled_buffer_74
  assign out_4 = comparator_21_eq ? {5{1'b1}} : 5'bz;  // Controlled_Buffer controlled_buffer_75
  assign out_4 = comparator_22_eq ? 5'b11110 : 5'bz;  // Controlled_Buffer controlled_buffer_76
  assign out_4 = comparator_23_eq ? {5{1'b1}} : 5'bz;  // Controlled_Buffer controlled_buffer_77
  assign out_4 = comparator_24_eq ? 5'b11011 : 5'bz;  // Controlled_Buffer controlled_buffer_78
  assign out_4 = comparator_25_eq ? 5'b11000 : 5'bz;  // Controlled_Buffer controlled_buffer_79
  assign out_4 = comparator_26_eq ? 5'b11001 : 5'bz;  // Controlled_Buffer controlled_buffer_80
  assign out_4 = comparator_27_eq ? {5{1'b0}} : 5'bz;  // Controlled_Buffer controlled_buffer_81
endmodule
